// Logisim project 4.1.circ as structural Verilog: 1 circuit, main circuit main
module main (
  input  W,
  input  X,
  input  Y,
  input  Z,
  output out_5
);

  wire nand_1_out, nand_2_out, nand_3_out, nand_4_out;

  nand nand_1 (nand_1_out, X, Y);
  nand nand_2 (nand_2_out, W, nand_1_out);
  nand nand_3 (nand_3_out, nand_1_out, Z);
  nand nand_4 (nand_4_out, nand_2_out, nand_3_out);
endmodule
