// Logisim project 4.3.circ as structural Verilog: 2 circuits, main circuit main
module main (
  input  A6,
  input  A5,
  input  A4,
  input  A3,
  input  A2,
  input  A1,
  input  A0,
  output One,
  output Two,
  output Four
);

  wire adder_1_cout, adder_1_out, adder_2_cout, adder_2_out, adder_3_cout;

  Adder #(.width(1)) adder_1 (.a(A5), .b(A4), .out(adder_1_out), .cin(A6), .cout(adder_1_cout));
  Adder #(.width(1)) adder_2 (.a(A2), .b(A1), .out(adder_2_out), .cin(A3), .cout(adder_2_cout));
  Adder #(.width(1)) adder_3 (.a(adder_2_out), .b(A0), .out(One), .cin(adder_1_out), .cout(adder_3_cout));
  Adder #(.width(1)) adder_4 (.a(adder_2_cout), .b(adder_1_cout), .out(Two), .cin(adder_3_cout), .cout(Four));
endmodule

module HA (
  input  A,
  input  B,
  output S,
  output C
);

  xor xor_1 (S, A, B);
  and and_1 (C, B, A);
endmodule
