// Logisim project F2.circ as structural Verilog: 1 circuit, main circuit main
module main (
  input  A,
  input  B,
  input  C,
  input  D,
  output out_5
);

  and and_1 (out_5, A, B, C, D);
endmodule
