// Logisim project shift.circ as structural Verilog: 1 circuit, main circuit main
module main (
  input  [1:0] S1andS0,
  input  B_in,
  output A7,
  output A6,
  output A5,
  output B_out,
  output A4,
  output A3,
  output A2,
  output A1,
  output A0
);

  wire and_1_out, clock_1_out, multiplexer_1_out, multiplexer_2_out, multiplexer_3_out, multiplexer_4_out,
       multiplexer_5_out, multiplexer_6_out, multiplexer_7_out, multiplexer_8_out, multiplexer_9_out,
       multiplexer_10_out, not_1_out;

  Clock clock_1 (.out(clock_1_out));
  Multiplexer #(.select(2), .enable("false")) multiplexer_1 (
    .in1(B_in), .in2(A6), .in3(A0), .out(multiplexer_1_out), .sel(S1andS0));  // open: in0
  Multiplexer #(.select(2), .enable("false")) multiplexer_2 (
    .in1(A7), .in2(A5), .in3(A7), .out(multiplexer_2_out), .sel(S1andS0));  // open: in0
  Multiplexer #(.select(2), .enable("false")) multiplexer_3 (
    .in1(A6), .in2(A4), .in3(A6), .out(multiplexer_3_out), .sel(S1andS0));  // open: in0
  Multiplexer #(.select(2), .enable("false")) multiplexer_4 (
    .in1(A5), .in2(A3), .in3(A5), .out(multiplexer_4_out), .sel(S1andS0));  // open: in0
  Multiplexer #(.select(2), .enable("false")) multiplexer_5 (
    .in1(A4), .in2(A2), .in3(A4), .out(multiplexer_5_out), .sel(S1andS0));  // open: in0
  Multiplexer #(.select(2), .enable("false")) multiplexer_6 (
    .in1(A3), .in2(A1), .in3(A3), .out(multiplexer_6_out), .sel(S1andS0));  // open: in0
  Multiplexer #(.select(2), .enable("false")) multiplexer_7 (
    .in1(A2), .in2(A0), .in3(A2), .out(multiplexer_7_out), .sel(S1andS0));  // open: in0
  Multiplexer #(.select(2), .enable("false")) multiplexer_8 (
    .in1(A1), .in2(B_in), .in3(A1), .out(multiplexer_8_out), .sel(S1andS0));  // open: in0
  Multiplexer #(.select(2), .enable("false")) multiplexer_9 (
    .in0(1'b1), .in1(1'b0), .in2(1'b0), .in3(1'b0), .out(multiplexer_9_out), .sel(S1andS0));
  not not_1 (not_1_out, multiplexer_9_out);
  and and_1 (and_1_out, clock_1_out, not_1_out);
  D_Flip_Flop d_ff_1 (.D(multiplexer_1_out), .clk(and_1_out), .Q(A7));  // open: Qn, preset, reset
  D_Flip_Flop d_ff_2 (.D(multiplexer_2_out), .clk(and_1_out), .Q(A6));  // open: Qn, preset, reset
  D_Flip_Flop d_ff_3 (.D(multiplexer_3_out), .clk(and_1_out), .Q(A5));  // open: Qn, preset, reset
  D_Flip_Flop d_ff_4 (.D(multiplexer_4_out), .clk(and_1_out), .Q(A4));  // open: Qn, preset, reset
  D_Flip_Flop d_ff_5 (.D(multiplexer_5_out), .clk(and_1_out), .Q(A3));  // open: Qn, preset, reset
  D_Flip_Flop d_ff_6 (.D(multiplexer_6_out), .clk(and_1_out), .Q(A2));  // open: Qn, preset, reset
  D_Flip_Flop d_ff_7 (.D(multiplexer_7_out), .clk(and_1_out), .Q(A1));  // open: Qn, preset, reset
  D_Flip_Flop d_ff_8 (.D(multiplexer_8_out), .clk(and_1_out), .Q(A0));  // open: Qn, preset, reset
  Multiplexer #(.select(2), .enable("false")) multiplexer_10 (
    .in1(A0), .in2(A7), .out(multiplexer_10_out), .sel(S1andS0));  // open: in0, in3
  D_Flip_Flop d_ff_9 (.D(multiplexer_10_out), .clk(and_1_out), .Q(B_out));  // open: Qn, preset, reset
endmodule
